# Fritzing sketch klima_Sketch_un (saved by Fritzing 0.9.3b)
breadboards: 1

parts:
  Part2 = Arduino Mega 2560 (Rev3)
  LED5 = LED - 5mm [color="White (8000K)" package="5 mm [THT]"]
  LED6 = LED - 5mm [color="Red (633nm)" package="5 mm [THT]"]
  LED7 = LED - 5mm [color="Green (555nm)" package="5 mm [THT]"]
  LED8 = LED - 5mm [color="Yellow (595nm)" package="5 mm [THT]"]
  R8 = Resistor [tolerance=±5% resistance=220 package=THT]
  R9 = Resistor [tolerance=±5% resistance=220 package=THT]
  R10 = Resistor [tolerance=±5% resistance=220 package=THT]
  R11 = Resistor [tolerance=±5% resistance=220 package=THT]
  R12 = Resistor [tolerance=±5% resistance=220 package=THT]
  RHT2 = Humidity and Temperature Sensor RHT03
  S2 = Pushbutton [package="[THT]"]
  R13 = Rotary Potentiometer (Large) [maximum_resistance=100kΩ package=THT]  # not connected

nets:
  N1: Part2.D12_PWM, R10.Pin_0
  N2: Part2.D11_PWM, R8.Pin_0
  N3: Part2.D10_PWM, R11.Pin_0
  N4: Part2.D9_PWM, R12.Pin_0
  N5: Part2.D8_PWM, S2.Pin_3, S2.Pin_4
  5V: Part2.5V, R9.Pin_0, RHT2.Vcc
  N6: Part2.GND, LED5.cathode, LED6.cathode, LED7.cathode, LED8.cathode, RHT2.GND_2, S2.Pin_1, S2.Pin_2
  N7: Part2.D7_PWM, R9.Pin_1, RHT2.Data-signal
  N8: LED5.anode, R10.Pin_1
  N9: LED6.anode, R12.Pin_1
  N10: LED7.anode, R11.Pin_1
  N11: LED8.anode, R8.Pin_1

notes:
  - Mega 2560
  - Breadboard
  - DHT11 sensor
  - Potentiometer
  - Knap
  - LED'er
  - Resistors
  - Wires
